# Fritzing sketch Water cooling controller (saved by Fritzing 0.9.9b)
circuit board: 13.7618cm x 12.5042cm
stripboards: 1

parts:
  FAN2 = Header 4 [package=molex-1x4_lock]
  FAN3 = Header 4 [package=molex-1x4_lock]
  TH2_(Outlet) = double row male pin header, 2 pins [form="♂ (male)"]
  TH1_(Inlet) = double row male pin header, 2 pins [form="♂ (male)"]
  J2 = female pin header, 15 pins [form="♀ (female)"]
  J1 = female pin header, 15 pins [form="♀ (female)"]
  R5 = Resistor [tolerance=±10% resistance=10k package=THT]
  2_8_TFT_SPI_240X320_V1_2 = male pin header, 9 pins [form="♂ (male)"]
  SATA_Power = male pin header, 5 pins [form="♂ (male)"]
  R4 = Resistor [tolerance=±10% resistance=10k package=THT]
  M1 = DOIT Esp32 DevKit v1 (30 pins long, 11 pins width) [part_number=ESP32S-PIN30]
  R6 = Resistor [tolerance=±10% resistance=3.3k package=THT]
  PUMP = Header 4 [package=molex-1x4_lock]
  FAN1 = Header 4 [package=molex-1x4_lock]

nets:
  N1: FAN2.1, FAN3.1, TH2_(Outlet).pin1, TH1_(Inlet).pin2, J2.pin14, J1.pin14, 2_8_TFT_SPI_240X320_V1_2.pin1, SATA_Power.pin2, SATA_Power.pin4, M1.GND, PUMP.1, FAN1.1
  N2: FAN2.2, FAN3.2, SATA_Power.pin5, PUMP.2, FAN1.2
  N3: FAN2.3, J2.pin9, M1.D26
  N4: FAN2.4, FAN3.4, J1.pin10, M1.RX2, PUMP.4, FAN1.4
  N5: FAN3.3, J2.pin10, M1.D27
  N6: TH2_(Outlet).pin2, J2.pin5, R5.Pin_1, M1.D35
  N7: TH1_(Inlet).pin1, J2.pin4, R4.Pin_1, M1.D34
  N8: J2.pin1, M1.EN
  N9: J2.pin2, M1.VP
  N10: J2.pin3, M1.VN
  N11: J2.pin6, M1.D32
  N12: J2.pin7, M1.D33
  N13: J2.pin8, M1.D25, FAN1.3
  N14: J2.pin11, M1.D14, R6.Pin_1, PUMP.3
  N15: J2.pin12, M1.D12
  N16: J2.pin13, M1.D13
  N17: J2.pin15, 2_8_TFT_SPI_240X320_V1_2.pin6, SATA_Power.pin3, M1.VIN
  N18: J1.pin1, 2_8_TFT_SPI_240X320_V1_2.pin2, M1.D23
  N19: J1.pin2, 2_8_TFT_SPI_240X320_V1_2.pin3, M1.D22
  N20: J1.pin3, M1.TX0
  N21: J1.pin4, M1.RX0
  N22: J1.pin5, M1.D21
  N23: J1.pin6, 2_8_TFT_SPI_240X320_V1_2.pin7, M1.D19
  N24: J1.pin7, 2_8_TFT_SPI_240X320_V1_2.pin8, M1.D18
  N25: J1.pin8, 2_8_TFT_SPI_240X320_V1_2.pin9, M1.D5
  N26: J1.pin9, M1.TX2
  N27: J1.pin11, 2_8_TFT_SPI_240X320_V1_2.pin4, M1.D4
  N28: J1.pin12, M1.D2
  N29: J1.pin13, 2_8_TFT_SPI_240X320_V1_2.pin5, M1.D15
  N30: J1.pin15, R5.Pin_0, SATA_Power.pin1, R4.Pin_0, M1.3V3, R6.Pin_0

notes:
  GND
  VCC
  RESET
  MOSI
  MISO
  DC
  LED
  SCK
  CS
  SENSE
  PWM
  NC
  3V
  5V
  12V

custom parts:
  DOIT Esp32 DevKit v1 (30 pins long, 11 pins width): The DOIT Esp32 DevKit v1 is one of the development board created by DOIT to evaluate the ESP-WROOM-32 module. It is based on the ESP32 microcontroller that boasts Wifi, Bluetooth, Ethernet and Low Power support all in a single chip. (vanepp) made breadboard work, adjusted pin numbering and labels and reduced size of schematic and cleaned up pcb. This chip is 30pins long (2 x15) and 11 pins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
